// Logisim project cpu.circ as structural Verilog: 3 circuits, main circuit main
module main (
  input  in_1,
  input  in_2
);

  wire clock_unit_1_aclk, clock_unit_1_mclk;

  LED led_1 (.in(clock_unit_1_mclk));
  LED led_2 (.in(clock_unit_1_aclk));
  Clock_Unit clock_unit_1 (.Sel(in_1), .Trigger(in_2), .MCLK(clock_unit_1_mclk), .ACLK(clock_unit_1_aclk));
  Timer_Unit timer_unit_1 ();  // open: CLK, TxCTR, TxCR, INTR
endmodule

module Timer_Unit (
  input  [1:0] CLK,
  input  [7:0] TxCTR,
  input  [15:0] TxCR,
  output INTR
);

  wire multiplexer_1_out, multiplexer_2_out;
  wire [6:0] counter_1_q;
  wire [15:0] counter_2_q, xnor_1_out;

  // Probe on TxCR
  Multiplexer multiplexer_1 (.in0(CLK[0]), .in1(CLK[1]), .out(multiplexer_1_out), .sel(TxCTR[7]));
  Counter #(.max('h7f), .width(7)) counter_1 (
    .clr(TxCTR[2]), .load(1'b0), .up(1'b1), .count(TxCTR[6]), .clk(multiplexer_1_out), .Q(counter_1_q));  // open: D, carry
  Multiplexer #(.select(3)) multiplexer_2 (
    .in0(multiplexer_1_out), .in1(counter_1_q[0]), .in2(counter_1_q[1]), .in3(counter_1_q[2]),
    .in4(counter_1_q[3]), .in5(counter_1_q[4]), .in6(counter_1_q[5]), .in7(counter_1_q[6]),
    .out(multiplexer_2_out), .sel(TxCTR[5:3]));
  Counter #(.max('hffff), .width(16)) counter_2 (
    .clr(TxCTR[2]), .load(1'b0), .up(1'b1), .count(TxCTR[6]), .clk(multiplexer_2_out), .Q(counter_2_q));  // open: D, carry
  assign xnor_1_out = ~(counter_2_q ^ TxCR);  // XNOR_Gate xnor_1, 16 bits wide
  and and_1 (INTR, xnor_1_out[0], xnor_1_out[1], xnor_1_out[2], xnor_1_out[3], xnor_1_out[4], xnor_1_out[5], xnor_1_out[6], xnor_1_out[7], xnor_1_out[8], xnor_1_out[9], xnor_1_out[10], xnor_1_out[11], xnor_1_out[12], xnor_1_out[13], xnor_1_out[14], xnor_1_out[15]);

  // Other names for the same wires on the sheet: CMP[15:0] = TxCR

  // Notes on the sheet:
  //   Divider
  //   Clear
  //   CLK Select
  //   Timer Enable
endmodule

module Clock_Unit (
  input  Sel,
  input  Trigger,
  output MCLK,
  output ACLK
);

  wire clock_1_out, clock_2_out;

  Clock clock_1 (.out(clock_1_out));
  Clock #(.highDuration(32), .lowDuration(32)) clock_2 (.out(clock_2_out));
  Multiplexer multiplexer_1 (.in0(Trigger), .in1(clock_1_out), .out(MCLK));  // open: sel
  Multiplexer multiplexer_2 (.in0(Trigger), .in1(clock_2_out), .out(ACLK));  // open: sel

  // Notes on the sheet:
  //   Master Clock 1MHz
  //   Auxiliary Clock 32KHz
endmodule
